// Logisim project Lab3circ1.circ as structural Verilog: 1 circuit, main circuit main
module main (
  input  in_1,
  input  in_2,
  input  in_3
);

  wire and_1_out, and_2_out, and_3_out, and_4_out, and_5_out, and_6_out, and_7_out, and_8_out, not_1_out,
       not_2_out, not_3_out;

  not not_1 (not_1_out, in_1);
  not not_2 (not_2_out, in_2);
  not not_3 (not_3_out, in_3);
  LED led_1 (.in(and_1_out));
  and and_1 (and_1_out, not_1_out, not_2_out, not_3_out);
  and and_2 (and_2_out, not_1_out, not_2_out, in_3);
  LED led_2 (.in(and_2_out));
  LED led_3 (.in(and_3_out));
  and and_3 (and_3_out, not_1_out, in_2, not_3_out);
  LED led_4 (.in(and_4_out));
  and and_4 (and_4_out, not_1_out, in_2, in_3);
  LED led_5 (.in(and_5_out));
  and and_5 (and_5_out, in_1, not_2_out, not_3_out);
  and and_6 (and_6_out, in_1, not_2_out, in_3);
  LED led_6 (.in(and_6_out));
  LED led_7 (.in(and_7_out));
  and and_7 (and_7_out, in_1, in_2, not_3_out);
  LED led_8 (.in(and_8_out));
  and and_8 (and_8_out, in_1, in_2, in_3);

  // Notes on the sheet:
  //   Octal Decoder
  //   L0
  //   L1
  //   L2
  //   L3
  //   L4
  //   L5
  //   L6
  //   L7
endmodule
