// Logisim project Lab3circ3.circ as structural Verilog: 1 circuit, main circuit main
module main (
  input  in_1,
  input  in_2,
  input  in_3,
  input  in_4,
  input  in_5,
  input  in_6,
  input  in_7,
  input  in_8,
  input  in_9
);

  wire and_1_out, and_2_out, and_3_out, and_4_out, and_5_out, and_6_out, and_7_out, and_8_out, not_1_out,
       or_1_out, or_2_out, or_3_out, or_4_out;

  not not_1 (not_1_out, in_1);
  and and_1 (and_1_out, not_1_out, in_3);
  and and_2 (and_2_out, not_1_out, in_2);
  and and_3 (and_3_out, not_1_out, in_4);
  or or_1 (or_1_out, and_2_out, and_5_out);
  LED led_1 (.in(or_1_out));
  and and_4 (and_4_out, not_1_out, in_5);
  or or_2 (or_2_out, and_1_out, and_6_out);
  LED led_2 (.in(or_2_out));
  and and_5 (and_5_out, in_1, in_6);
  or or_3 (or_3_out, and_3_out, and_8_out);
  LED led_3 (.in(or_3_out));
  and and_6 (and_6_out, in_1, in_7);
  or or_4 (or_4_out, and_4_out, and_7_out);
  LED led_4 (.in(or_4_out));
  and and_7 (and_7_out, in_1, in_9);
  and and_8 (and_8_out, in_1, in_8);

  // Notes on the sheet:
  //   Right
  //   Nibble Multiplexer - 2 to 1
  //   A2
  //   A3
  //   A1
  //   A0
  //   B3
  //   B2
  //   B0
  //   B1
endmodule
