// Logisim project Lab3circ4.circ as structural Verilog: 1 circuit, main circuit main
module main (
  input  in_1,
  input  in_2,
  input  in_3,
  input  in_4,
  input  in_5,
  input  in_6,
  input  in_7,
  input  in_8,
  input  in_9
);

  wire [3:0] multiplexer_1_out;

  LED led_1 (.in(multiplexer_1_out[3]));
  Multiplexer #(.width(4), .enable("false")) multiplexer_1 (
    .in0({in_2, in_3, in_4, in_5}), .in1({in_6, in_7, in_8, in_9}), .out(multiplexer_1_out), .sel(in_1));
  LED led_2 (.in(multiplexer_1_out[2]));
  LED led_3 (.in(multiplexer_1_out[1]));
  LED led_4 (.in(multiplexer_1_out[0]));

  // Notes on the sheet:
  //   Right
  //   Nibble Multiplexer - 2 to 1
  //   A2
  //   A3
  //   A1
  //   A0
  //   B3
  //   B2
  //   B0
  //   B1
endmodule
