// Logisim project Lab3circ5.circ as structural Verilog: 1 circuit, main circuit main
module main (
  input  in_1,
  input  in_2,
  input  in_3,
  input  in_4,
  input  in_5,
  input  in_6,
  input  in_7,
  input  in_8,
  input  in_9
);

  wire controlled_buffer_1_out, controlled_buffer_2_out, controlled_buffer_3_out, controlled_buffer_4_out;

  not not_1 (in_2, in_1);
  assign controlled_buffer_1_out = in_2 ? in_2 : 1'bz;  // Controlled_Buffer controlled_buffer_1
  assign controlled_buffer_2_out = in_2 ? in_2 : 1'bz;  // Controlled_Buffer controlled_buffer_2
  assign controlled_buffer_3_out = in_2 ? in_2 : 1'bz;  // Controlled_Buffer controlled_buffer_3
  LED led_1 (.in(controlled_buffer_2_out));
  assign controlled_buffer_4_out = in_2 ? in_2 : 1'bz;  // Controlled_Buffer controlled_buffer_4
  LED led_2 (.in(controlled_buffer_1_out));
  assign controlled_buffer_2_out = in_1 ? in_1 : 1'bz;  // Controlled_Buffer controlled_buffer_5
  LED led_3 (.in(controlled_buffer_3_out));
  assign controlled_buffer_1_out = in_1 ? in_1 : 1'bz;  // Controlled_Buffer controlled_buffer_6
  LED led_4 (.in(controlled_buffer_4_out));
  assign controlled_buffer_4_out = in_1 ? in_1 : 1'bz;  // Controlled_Buffer controlled_buffer_7
  assign controlled_buffer_3_out = in_1 ? in_1 : 1'bz;  // Controlled_Buffer controlled_buffer_8

  assign in_3 = in_2;
  assign in_4 = in_2;
  assign in_5 = in_2;
  assign in_6 = in_1;
  assign in_7 = in_1;
  assign in_8 = in_1;
  assign in_9 = in_1;

  // Notes on the sheet:
  //   Right
  //   Nibble Bus with Drivers
  //   A2
  //   A3
  //   A1
  //   A0
  //   B3
  //   B2
  //   B0
  //   B1
endmodule
