// Logisim project octalDecoderSkel.circ as structural Verilog: 1 circuit, main circuit main
module main (
  input  in_1,
  input  in_2,
  input  in_3
);

  wire undriven, undriven_2, undriven_3, undriven_4, undriven_5, undriven_6, undriven_7, undriven_8;

  LED led_1 (.in(undriven));
  LED led_2 (.in(undriven_2));
  LED led_3 (.in(undriven_3));
  LED led_4 (.in(undriven_4));
  LED led_5 (.in(undriven_5));
  LED led_6 (.in(undriven_6));
  LED led_7 (.in(undriven_7));
  LED led_8 (.in(undriven_8));

  // Notes on the sheet:
  //   Octal Decoder
  //   L0
  //   L1
  //   L2
  //   L3
  //   L4
  //   L5
  //   L6
  //   L7
endmodule
