// Logisim project 8bitinverter.circ as structural Verilog: 1 circuit, main circuit main
module main (
  input  in_1,
  input  in_2,
  input  in_3,
  input  in_4,
  input  in_5,
  input  in_6,
  input  in_7,
  input  in_8,
  input  in_9,
  input  in_10,
  input  in_11,
  input  in_12,
  input  in_13,
  input  in_14,
  input  in_15,
  input  in_16,
  input  in_17
);

  wire adder_1_cout, and_1_out, and_2_out, not_1_out, not_2_out, not_3_out;
  wire [7:0] adder_1_out, xor_1_out;

  not not_1 (not_1_out, in_1);
  xor xor_1 (xor_1_out[0], in_2, not_1_out);
  xor xor_2 (xor_1_out[1], in_3, not_1_out);
  xor xor_3 (xor_1_out[2], in_4, not_1_out);
  xor xor_4 (xor_1_out[3], in_5, not_1_out);
  xor xor_5 (xor_1_out[4], in_6, not_1_out);
  xor xor_6 (xor_1_out[5], in_7, not_1_out);
  xor xor_7 (xor_1_out[6], in_8, not_1_out);
  xor xor_8 (xor_1_out[7], in_9, not_1_out);
  Adder adder_1 (
    .a(xor_1_out), .b({in_17, in_16, in_15, in_14, in_13, in_12, in_11, in_10}), .out(adder_1_out),
    .cin(not_1_out), .cout(adder_1_cout));
  and and_1 (and_1_out, adder_1_cout, not_2_out);
  not not_2 (not_2_out, not_1_out);
  not not_3 (not_3_out, adder_1_cout);
  and and_2 (and_2_out, not_3_out, not_1_out);
  LED led_1 (.in(adder_1_out[0]));
  LED led_2 (.in(adder_1_out[1]));
  LED led_3 (.in(adder_1_out[2]));
  LED led_4 (.in(adder_1_out[3]));
  LED led_5 (.in(adder_1_out[4]));
  LED led_6 (.in(adder_1_out[5]));
  LED led_7 (.in(adder_1_out[6]));
  LED led_8 (.in(adder_1_out[7]));
  LED led_9 (.in(and_1_out));
  LED led_10 (.in(and_2_out));
endmodule
