// Logisim project regbus.circ as structural Verilog: 1 circuit, main circuit main
module main (
  input  L1,
  input  L2,
  input  E1,
  input  E2,
  input  L3,
  input  L4,
  input  E4,
  input  E3,
  output [7:0] out_9
);

  wire clock_1_out;
  wire [7:0] _1_q, _2_q, _3_q, _4_q;

  Register _1 (.D(out_9), .en(L1), .Q(_1_q), .clk(clock_1_out));  // open: clr
  assign out_9 = E1 ? _1_q : 8'bz;  // Controlled_Buffer controlled_buffer_1
  assign out_9 = E3 ? _3_q : 8'bz;  // Controlled_Buffer controlled_buffer_2
  Register _3 (.D(out_9), .en(L3), .Q(_3_q), .clk(clock_1_out));  // open: clr
  Clock clock_1 (.out(clock_1_out));
  Register _4 (.D(out_9), .en(L4), .Q(_4_q), .clk(clock_1_out));  // open: clr
  Register _2 (.D(out_9), .en(L2), .Q(_2_q), .clk(clock_1_out));  // open: clr
  assign out_9 = E2 ? _2_q : 8'bz;  // Controlled_Buffer controlled_buffer_3
  assign out_9 = E4 ? _4_q : 8'bz;  // Controlled_Buffer controlled_buffer_4
endmodule
