// Logisim project lab1logisim.circ as structural Verilog: 1 circuit, main circuit main
module main (
  input  in_1,
  input  in_2,
  input  in_3,
  input  in_4,
  input  in_5,
  input  in_6,
  input  in_7,
  input  in_8,
  input  in_9,
  input  in_10,
  input  in_11,
  input  in_12,
  input  in_13,
  input  in_14,
  input  in_15,
  input  in_16,
  input  in_17
);

  wire and_1_out, and_2_out, and_3_out, and_4_out, and_5_out, and_6_out, and_7_out, and_8_out, not_1_out,
       not_2_out, not_3_out, not_4_out, not_5_out, not_6_out, not_7_out, not_8_out, not_9_out, not_10_out,
       not_11_out, not_12_out;

  not not_1 (not_1_out, in_1);
  not not_2 (not_2_out, in_3);
  not not_3 (not_3_out, in_5);
  not not_4 (not_4_out, in_6);
  not not_5 (not_5_out, in_8);
  not not_6 (not_6_out, in_10);
  not not_7 (not_7_out, in_12);
  not not_8 (not_8_out, in_13);
  not not_9 (not_9_out, in_14);
  not not_10 (not_10_out, in_15);
  not not_11 (not_11_out, in_16);
  not not_12 (not_12_out, in_17);
  LED led_1 (.in(not_1_out));
  LED led_2 (.in(not_2_out));
  LED led_3 (.in(not_3_out));
  LED led_4 (.in(not_4_out));
  LED led_5 (.in(not_5_out));
  LED led_6 (.in(not_6_out));
  and and_1 (and_1_out, in_12, in_13);
  LED led_7 (.in(and_1_out));
  and and_2 (and_2_out, in_14, in_15);
  LED led_8 (.in(and_2_out));
  LED led_9 (.in(and_3_out));
  and and_3 (and_3_out, in_16, in_17);
  and and_4 (and_4_out, not_11_out, not_12_out);
  LED led_10 (.in(and_4_out));
  not not_13 (in_9, in_11);
  LED led_11 (.in(and_5_out));
  and and_5 (and_5_out, in_2, in_9);
  LED led_12 (.in(and_6_out));
  and and_6 (and_6_out, in_4, in_9);
  and and_7 (and_7_out, in_7, in_9);
  LED led_13 (.in(and_7_out));
  and and_8 (and_8_out, in_9, in_9);
  LED led_14 (.in(and_8_out));
endmodule
