// Logisim project lab2logisim.circ as structural Verilog: 1 circuit, main circuit main
module main (
  input  in_1,
  input  in_2,
  input  in_3,
  input  in_4,
  input  in_5,
  input  in_6,
  input  in_7,
  input  in_8,
  input  in_9,
  input  in_10,
  input  in_11,
  input  in_12,
  input  in_13,
  input  in_14,
  input  in_15,
  input  in_16,
  input  in_17,
  input  in_18,
  input  in_19,
  input  in_20,
  input  in_21,
  input  in_22,
  input  in_23,
  input  in_24,
  input  in_25,
  input  in_26,
  input  in_27
);

  wire and_1_out, and_2_out, and_3_out, nand_1_out, nand_2_out, nand_3_out, nand_4_out, nor_1_out, nor_2_out,
       nor_3_out, nor_4_out, not_1_out, or_1_out, or_2_out, or_3_out, or_4_out, or_5_out;

  or or_1 (or_1_out, in_1, in_3);
  or or_2 (or_2_out, in_5, in_7);
  or or_3 (or_3_out, in_9, in_11);
  or or_4 (or_4_out, in_13, in_15);
  nor nor_1 (nor_1_out, in_17, in_19);
  nor nor_2 (nor_2_out, in_21, in_22);
  nor nor_3 (nor_3_out, in_23, in_24);
  nor nor_4 (nor_4_out, in_25, in_27);
  LED led_1 (.in(or_1_out));
  LED led_2 (.in(or_2_out));
  LED led_3 (.in(or_3_out));
  LED led_4 (.in(or_4_out));
  LED led_5 (.in(nor_1_out));
  LED led_6 (.in(nor_2_out));
  LED led_7 (.in(nor_3_out));
  LED led_8 (.in(nor_4_out));
  not not_1 (not_1_out, in_20);
  LED led_9 (.in(nand_1_out));
  nand nand_1 (nand_1_out, in_2, in_4);
  LED led_10 (.in(nand_2_out));
  nand nand_2 (nand_2_out, in_6, in_8);
  LED led_11 (.in(nand_3_out));
  nand nand_3 (nand_3_out, in_10, in_12);
  nand nand_4 (nand_4_out, in_14, in_16);
  LED led_12 (.in(nand_4_out));
  and and_1 (and_1_out, in_18, in_20);
  and and_2 (and_2_out, not_1_out, in_26);
  and and_3 (and_3_out, in_18, in_26);
  LED led_13 (.in(or_5_out));
  or or_5 (or_5_out, and_1_out, and_2_out, and_3_out);
endmodule
